# Fritzing sketch devre (saved by Fritzing 0.9.3b)
breadboards: 1

parts:
  T3_Vakfı1 = Generic shrouded header - 32 pins [package=THT]
  Parça1 = RFID-RC522-v2
  J1 = Piezo Speaker

nets:
  N1: T3_Vakfı1.pin13, J1.pin2
  N2: T3_Vakfı1.pin16, J1.pin1
  N3: T3_Vakfı1.pin17, Parça1.GND
  N4: T3_Vakfı1.pin18, Parça1.3.3V
  N5: T3_Vakfı1.pin24, Parça1.MOSI
  N6: T3_Vakfı1.pin25, Parça1.MISO
  N7: T3_Vakfı1.pin26, Parça1.SCK
  N8: T3_Vakfı1.pin27, Parça1.SDA
  N9: T3_Vakfı1.pin31, Parça1.RST

notes:
  SDA-D4
  SCK-SCK
  MOSI-MOSI
  MISO-MISO
  GND-GND
  RST-D0
  3v3-3v3
  BuzzerGND-GND
  BuzzerSignal-D12

custom parts:
  Generic shrouded header - 32 pins: Ülkemizin mühendislik kaynakları kullanılarak geliştirilen Deneyap Kart; güçlü işlemcisi, dayanıklı tasarımı ve çok yönlü giriş/çıkış pinleri ile kullanıcılara Elektronik Programlama, Nesnelerin İnterneti (IoT) ve Yapay Zeka alanlarında başlangıç seviyesinden endüstriyel uygulamalara kadar her seviyede projeyi yapma imkanı sunuyor.
  RFID-RC522-v2: A simple China made RFID-RC522 Reader; do check the pin labels, as this is a MFRC522 based clone.
